# Fritzing sketch p13_potenziometro e led (saved by Fritzing 0.9.3b)
breadboards: 1

parts:
  Componente1 = Arduino Uno (Rev3)
  R2 = Resistor [tolerance=±5% resistance=220 package=THT]
  R3 = Rotary Potentiometer (Small) [maximum_resistance=100kΩ package=THT]
  LED1 = LED - 5mm [color="Red (633nm)" package="5 mm [THT]"]

nets:
  N1: Componente1.A0, R3.wiper
  N2: Componente1.GND, R3.leg2, LED1.cathode
  N3: Componente1.D3_PWM, R2.Pin_1
  N4: Componente1.5V, R3.leg1
  N5: R2.Pin_0, LED1.anode
